# Fritzing sketch Dome_Schematic (saved by Fritzing 0.8.7b)

parts:
  Mega = Arduino Mega 2560 (Rev3)
  M1 = DC Motor
  LED1 = LED - 5mm [color="Blue (470nm)" package="5 mm [THT]"]
  LED2 = LED - 5mm [color="Red (633nm)" package="5 mm [THT]"]
  LED3 = LED - 5mm [color="White (8000K)" package="5 mm [THT]"]
  LED4 = LED - 5mm [color="White (8000K)" package="5 mm [THT]"]
  LED5 = LED - 5mm [color="Red (633nm)" package="5 mm [THT]"]
  Q2 = Basic FET N-Channel [package="TO220 [THT]"]
  R2 = Resistor [tolerance=±5% resistance=47k package=THT]
  R3 = Resistor [tolerance=±5% resistance=1.2 package=THT]
  R4 = Resistor [tolerance=±5% resistance=0.1 package=THT]
  R5 = Resistor [tolerance=±5% resistance=1.2 package=THT]
  Q3 = Basic FET N-Channel [package="TO220 [THT]"]
  R6 = Resistor [tolerance=±5% resistance=47k package=THT]
  Q4 = Basic FET N-Channel [package="TO220 [THT]"]
  R7 = Resistor [tolerance=±5% resistance=47k package=THT]
  Q7 = Basic FET N-Channel [package="TO220 [THT]"]
  R10 = Resistor [tolerance=±5% resistance=47k package=THT]
  R12 = Resistor [tolerance=±5% resistance=1.2 package=THT]
  Ethernet_Shield = Arduino Ethernet Shield (Rev3)
  Q8 = NPN-Transistor [package="TO92 [THT]"]
  R13 = Resistor [tolerance=±5% resistance=330 package=THT]
  K1 = Relay [part_number=FRS1B-S package=THT]
  Soil_Moisture = SLIDER [package=slider]
  Buck_Conv = DC-DC_CONVERTER [package=dc-dc_converter]

nets:
  N1: Mega.A0, Buck_Conv.VOUT
  LEDs: Mega.A1, Mega.A2, Mega.A3, Mega.A4
  N2: Mega.A5, Soil_Moisture.S
  GND: Mega.GND, Q2.source, R2.Pin_1, Q3.source, R6.Pin_1, Q4.source, Q7.source, Q8.E, K1.A, Soil_Moisture.A, Buck_Conv.GND2
  N3: Mega.D13_PWM, Ethernet_Shield.SPI/D13
  N4: Mega.D12_PWM, Ethernet_Shield.SPI/D12
  N5: Mega.D11_PWM, Ethernet_Shield.PWM_D11
  N6: Mega.D10_PWM, Ethernet_Shield.ETH_CS
  N7: Mega.D9_PWM, Q4.gate, R7.Pin_0
  N8: Mega.D8_PWM, Q7.gate
  N9: Mega.5V, Soil_Moisture.E
  N10: Mega.D4_PWM, Ethernet_Shield.SDCS
  N11: Mega.D6_PWM, Q3.gate, R6.Pin_0
  N12: Mega.D7_PWM, Q2.gate, R2.Pin_0
  N13: Mega.D22, R13.Pin_0
  N14: M1.pin_1, LED5.anode, K1.COIL2
  N15: M1.pin_2, K1.B
  A2: LED1.cathode, R3.Pin_0
  N16: LED1.anode, LED2.anode, LED3.anode
  A3: LED2.cathode, R5.Pin_0
  A1: LED3.cathode, LED4.cathode, R4.Pin_0
  A4: LED5.cathode, R12.Pin_0
  N17: Q2.drain, R3.Pin_1
  N18: R4.Pin_1, Q3.drain
  N19: R5.Pin_1, Q4.drain
  N20: R7.Pin_1, R10.Pin_1
  N21: Q7.drain, R12.Pin_1
  N22: Q8.B, R13.Pin_1
  N23: Q8.C, K1.COIL1, K1.C1, K1.C2
  5V: Buck_Conv.VIN
  GND_2: Buck_Conv.GND1

custom parts:
  DC-DC_CONVERTER: APTS006A0X-SRZ Step-down 6A variable voltage switching module (TOL-09275)
